# Fritzing sketch circuito (saved by Fritzing 0.9.2b)
breadboards: 1

parts:
  LCD1 = LCD screen
  R1 = Rotary Potentiometer (Small) [maximum_resistance=100kΩ package=THT]
  T1 = TMP36 Temperature Sensor [package="TO92 [THT]"]
  R2 = Resistor [tolerance=±5% resistance=220 package=THT]
  Parte2 = Arduino Ethernet Shield (Rev3)

nets:
  GND: LCD1.VSS, LCD1.R/W, LCD1.LED-, R1.leg2, T1.GND, Parte2.GND
  VDD: LCD1.VDD, R1.leg1, R2.Pin_0, Parte2.5V
  N1: LCD1.V0, R1.wiper
  N2: LCD1.RS, Parte2.D8
  N3: LCD1.E, Parte2.PWM_D9
  N4: LCD1.DB4, Parte2.PWM_D6
  N5: LCD1.DB5, Parte2.PWM_D5
  N6: LCD1.DB6, Parte2.PWM_D3
  N7: LCD1.DB7, Parte2.D2
  N8: LCD1.LED+, R2.Pin_1
  N9: T1.+Vs, Parte2.3V3
  N10: T1.Vout, Parte2.A0
